# Fritzing sketch AlarmPi (saved by Fritzing 0.9.3b)
circuit board: 10.3cm x 6.37cm
breadboards: 1

parts:
  Raspberry_P1 = double row female pin header, 40 pins [form="♀ (female)"]
  LED_out = screw terminal, 4 pins
  keys = screw terminal, 4 pins
  Pad1 = Pad [width=30 height=30 connect=center]  # not connected
  PCA9685 = female pin header, 6 pins [form="♀ (female)"]
  J5 = female pin header, 4 pins [form="♀ (female)"]  # not connected
  J6 = female pin header, 4 pins [form="♀ (female)"]  # not connected
  J7 = female pin header, 4 pins [form="♀ (female)"]  # not connected
  Pad2 = Pad [width=30 height=30 connect=center]  # not connected
  J8 = female pin header, 4 pins [form="♀ (female)"]  # not connected
  J9 = female pin header, 4 pins [form="♀ (female)"]  # not connected
  J10 = female pin header, 4 pins [form="♀ (female)"]  # not connected
  J11 = female pin header, 4 pins [form="♀ (female)"]  # not connected
  J12 = female pin header, 4 pins [form="♀ (female)"]  # not connected
  J13 = female pin header, 4 pins [form="♀ (female)"]  # not connected
  J14 = female pin header, 4 pins [form="♀ (female)"]  # not connected
  J15 = female pin header, 4 pins [form="♀ (female)"]  # not connected
  J16 = female pin header, 4 pins [form="♀ (female)"]
  U1 = Voltage Regulator - 5V [package="TO220 [THT]"]
  5V+_out = Screw terminal - 2 pins [package=THT]
  LED1_IN- = female pin header, 1 pin [form="♀ (female)"]
  LED1_IN+ = female pin header, 1 pin [form="♀ (female)"]
  LED0_IN- = female pin header, 1 pin [form="♀ (female)"]
  LED0_IN+ = female pin header, 1 pin [form="♀ (female)"]
  12V+_in = screw terminal, 2 pins
  LED0_PWM = female pin header, 1 pin [form="♀ (female)"]
  LED1_PWM = female pin header, 1 pin [form="♀ (female)"]
  5V = female pin header, 2 pins [form="♀ (female)"]
  SPI_out = screw terminal, 3 pins
  C1 = Electrolytic Capacitor [capacitance=4.7µF package="100 mil [THT, electrolytic]"]
  C2 = Ceramic Capacitor [capacitance=220nF package="100 mil [THT, multilayer]"]
  C3 = Ceramic Capacitor [capacitance=220nF package="100 mil [THT, multilayer]"]
  LED1_OUT+ = female pin header, 1 pin [form="♀ (female)"]
  LED1_OUT- = female pin header, 1 pin [form="♀ (female)"]
  LED0_OUT+ = female pin header, 1 pin [form="♀ (female)"]
  LED0_OUT- = female pin header, 1 pin [form="♀ (female)"]
  IC1 = IC, DIP package, 4 pins [chip_label=IC]
  R1 = Resistor [tolerance=±5% resistance=470 package=THT]
  USB_5V+ = female pin header, 1 pin [form="♀ (female)"]
  J20 = female pin header, 1 pin [form="♀ (female)"]  # not connected
  J21 = female pin header, 1 pin [form="♀ (female)"]  # not connected
  USB_GND = female pin header, 1 pin [form="♀ (female)"]
  R2 = Resistor [tolerance=±5% resistance=1k package=THT]

nets:
  N1: Raspberry_P1.pin7, keys.pin1, C2.0
  N2: Raspberry_P1.pin8, R1.Pin_1
  N3: Raspberry_P1.pin9, keys.pin2, C2.1
  N4: Raspberry_P1.pin10, keys.pin3, C3.1
  N5: Raspberry_P1.pin11, keys.pin4, C3.0
  N6: Raspberry_P1.pin18, PCA9685.pin5, R2.Pin_1
  N7: Raspberry_P1.pin21, PCA9685.pin6, U1.GND, 5V+_out.pin1, LED1_IN-.pin1, LED0_IN-.pin1, 12V+_in.pin1, 5V.pin1, SPI_out.pin1, C1.-, IC1.pin2, USB_GND.pin1
  N8: Raspberry_P1.pin29, SPI_out.pin2
  N9: Raspberry_P1.pin31, SPI_out.pin3
  N10: Raspberry_P1.pin38, PCA9685.pin4
  N11: Raspberry_P1.pin39, PCA9685.pin3
  N12: Raspberry_P1.pin40, R2.Pin_0
  N13: LED_out.pin1, LED1_OUT-.pin1
  N14: LED_out.pin2, LED1_OUT+.pin1
  N15: LED_out.pin3, LED0_OUT-.pin1
  N16: LED_out.pin4, LED0_OUT+.pin1
  N17: PCA9685.pin1, PCA9685.pin2, U1.output_voltage, 5V+_out.pin2, 5V.pin2, C1.+, IC1.pin4
  N18: J16.pin3, LED1_PWM.pin1
  N19: J16.pin4, LED0_PWM.pin1
  N20: U1.input_voltage, LED1_IN+.pin1, LED0_IN+.pin1, 12V+_in.pin2
  N21: IC1.pin1, R1.Pin_0
  N22: IC1.pin3, USB_5V+.pin1

notes:
  5V+
  AlarmPi
  LED1 driver
  LED0 driver
  USB 5V out sound
  Raspberry
  12V Supply
  gpio23
  GND
  gpio24
  gpio25
  gpio16
  3,3V
  IIC SDA
  IIC SCL
  SPI MOSI
  SPI SCLK
